// Logisim project s-mips.circ as structural Verilog
module S_MIPS_Board (
  input  DESHABILITAR_DISPATCHER,
  output halt
);

  wire button_1_out, CLK, CS, d_ff_1_q, LCLR, LoadRAM, LoadRAMOn, LW, R_R_W, R_W, ram_dispatcher_1_finished,
       RCS, Reset_out, RST, TTY_EN;
  wire [2:0] KDB;
  wire [3:0] LMask, Mask, ram_1_read_time, ram_1_write_time, RMask;
  wire [6:0] KDB_DATA, TTY_DATA;
  wire [15:0] Addr, LAddr, RAddr;
  wire [31:0] I0, I1, I2, I3, LData, ram_1_data_out_0, ram_1_data_out_1, ram_1_data_out_2, ram_1_data_out_3,
       RI0, RI1, RI2, RI3;

  TTY #(.rows(25), .cols(80)) tty_1 (.data(TTY_DATA), .clk(CLK), .we(TTY_EN), .clr(RST));
  not not_1 (LoadRAMOn, ram_dispatcher_1_finished);
  RAM_Dispatcher ram_dispatcher_1 (
    .WriteTime(ram_1_write_time), .Clock(CLK), .Data(LData), .Address(LAddr), .Mask(LMask),
    .Finished(ram_dispatcher_1_finished), .Write(LW), .CLR(LCLR));
  Keyboard #(.buflen(64)) keyboard_1 (.clk(CLK), .re(KDB[0]), .avail(KDB[2]), .data(KDB_DATA));  // open: clr
  RAM ram_1 (
    .Address(RAddr), .Data_Out_0(ram_1_data_out_0), .Data_Out_1(ram_1_data_out_1),
    .Data_Out_2(ram_1_data_out_2), .Data_Out_3(ram_1_data_out_3), .Data_In_0(RI0), .Data_In_1(RI1),
    .Data_In_2(RI2), .Data_In_3(RI3), .Mask(RMask), .nRead_Write(R_R_W), .Chip_Select(RCS),
    .Read_Time(ram_1_read_time), .Reset(button_1_out), .Write_Time(ram_1_write_time));
  Button button_1 (.out(button_1_out));
  D_Flip_Flop d_ff_1 (.clk(CLK), .D(1'b1), .Q(d_ff_1_q), .reset(Reset_out));  // open: Qn, preset, en
  Button Reset (.out(Reset_out));
  S_MIPS s_mips_1 (
    .Address(Addr), .Kbd_Clear(KDB[1]), .Kbd_Available(KDB[2]), .RAM_In_0(I0), .Kbd_ASCII_Data(KDB_DATA),
    .RAM_In_1(I1), .RAM_In_2(I2), .RAM_In_3(I3), .Reset(RST), .RAM_Out_0(ram_1_data_out_0), .Clock(CLK),
    .RAM_Out_1(ram_1_data_out_1), .Stop(halt), .RAM_Out_2(ram_1_data_out_2), .RAM_Out_3(ram_1_data_out_3),
    .Mask(Mask), .Read_Time(ram_1_read_time), .Write_Time(ram_1_write_time), .nRead_Write(R_W),
    .Chip_Select(CS), .TTY_Enable(TTY_EN), .TTY_ASCII_Data(TTY_DATA), .Kbd_Enable(KDB[0]));
  D_Flip_Flop d_ff_2 (.clk(CLK), .D(d_ff_1_q), .Qn(LCLR), .reset(Reset_out));  // open: Q, preset, en
  or or_1 (RST, LCLR, LoadRAM);
  Clock clock_1 (.out(CLK));
  Multiplexer #(.width(32), .enable("false")) multiplexer_1 (.in0(I0), .in1(LData), .out(RI0), .sel(LoadRAM));
  Multiplexer #(.width(32), .enable("false")) multiplexer_2 (.in0(I1), .in1(LData), .out(RI1), .sel(LoadRAM));
  Multiplexer #(.width(32), .enable("false")) multiplexer_3 (.in0(I2), .in1(LData), .out(RI2), .sel(LoadRAM));
  Multiplexer #(.width(32), .enable("false")) multiplexer_4 (.in0(I3), .in1(LData), .out(RI3), .sel(LoadRAM));
  and and_1 (LoadRAM, ~DESHABILITAR_DISPATCHER, LoadRAMOn);  // AND_Gate
  Multiplexer #(.width(16), .enable("false")) multiplexer_5 (.in0(Addr), .in1(LAddr), .out(RAddr), .sel(LoadRAM));
  Multiplexer #(.width(4), .enable("false")) multiplexer_6 (.in0(Mask), .in1(LMask), .out(RMask), .sel(LoadRAM));
  Multiplexer #(.enable("false")) multiplexer_7 (.in0(CS), .in1(LW), .out(RCS), .sel(LoadRAM));
  Multiplexer #(.enable("false")) multiplexer_8 (.in0(R_W), .in1(LW), .out(R_R_W), .sel(LoadRAM));

  // Notes on the sheet:
  //   NO MODIFICAR
  //   Keyboard
endmodule

module RAM (
  input  [15:0] Address,
  input  [31:0] Data_In_0,
  input  [31:0] Data_In_1,
  input  [31:0] Data_In_2,
  input  [31:0] Data_In_3,
  input  [3:0] Mask,
  input  nRead_Write,
  input  Chip_Select,
  input  Reset,
  output [31:0] Data_Out_0,
  output [31:0] Data_Out_1,
  output [31:0] Data_Out_2,
  output [31:0] Data_Out_3,
  output [3:0] Read_Time,
  output [3:0] Write_Time
);

  wire and_2_out, and_3_out, and_4_out, and_5_out, and_6_out, and_7_out, and_8_out, and_9_out, Changed, CLK,
       comparator_2_eq, comparator_3_eq, comparator_4_eq, comparator_5_eq, comparator_6_eq, Count,
       demultiplexer_3_out0, Idle, Idle_q, Load, Load0, Load1, nand_1_out, or_1_out, or_2_out, or_3_out,
       or_4_out, or_5_out, or_6_out, or_7_out, or_8_out, or_9_out, or_10_out, Proc_q, Update_Mem, Zero_Time;
  wire [3:0] counter_1_q, multiplexer_1_out, subtractor_1_out;
  wire [31:0] register_1_q, register_2_q, register_3_q, register_4_q, register_5_q;

  // Probe on 4'b0011
  // Probe on 4'b0010
  Multiplexer #(.width(4), .enable("false")) multiplexer_1 (
    .in0(4'b0011), .in1(4'b0010), .out(multiplexer_1_out), .sel(nRead_Write));
  or or_1 (or_1_out, Idle, Update_Mem);
  or or_2 (or_2_out, ~Chip_Select, Reset);  // OR_Gate
  Subtractor #(.width(4)) subtractor_1 (.a(multiplexer_1_out), .b(4'b0010), .out(subtractor_1_out));  // open: bin, bout
  Demultiplexer #(.enable("false")) demultiplexer_1 (.out0(Idle), .out1(Load0), .in(Idle_q), .sel(Changed));
  D_Flip_Flop u_Idle (.clk(CLK), .D(or_1_out), .Q(Idle_q), .preset(or_2_out));  // open: Qn, en, reset
  // Probe on counter_1_q
  Counter #(.width(4), .max('hf)) counter_1 (
    .load(Load), .D(subtractor_1_out), .count(Count), .Q(counter_1_q), .clk(CLK), .clr(or_3_out));  // open: carry
  or or_3 (or_3_out, ~Chip_Select, Reset);  // OR_Gate
  Comparator #(.width(4), .mode("unsigned")) comparator_1 (
    .a(4'b0000), .b(counter_1_q), .eq(Zero_Time));  // open: gt, lt
  or or_4 (or_4_out, Count, Load0, Load1);
  Register #(.width(32)) register_1 (.D(Data_In_0), .en(Chip_Select), .Q(register_1_q), .clk(CLK), .clr(or_5_out));
  or or_5 (or_5_out, ~Chip_Select, Reset);  // OR_Gate
  Register #(.width(32)) register_2 (.D(Data_In_1), .en(Chip_Select), .Q(register_2_q), .clk(CLK), .clr(or_6_out));
  or or_6 (or_6_out, ~Chip_Select, Reset);  // OR_Gate
  Register #(.width(32)) register_3 (.D(Data_In_2), .en(Chip_Select), .Q(register_3_q), .clk(CLK), .clr(or_7_out));
  or or_7 (or_7_out, ~Chip_Select, Reset);  // OR_Gate
  Register #(.width(32)) register_4 (.D(Data_In_3), .en(Chip_Select), .Q(register_4_q), .clk(CLK), .clr(or_8_out));
  or or_8 (or_8_out, ~Chip_Select, Reset);  // OR_Gate
  Register #(.width(32)) register_5 (
    .D({{11{1'b1}}, nRead_Write, Mask, Address}), .en(Chip_Select), .Q(register_5_q), .clk(CLK),
    .clr(or_9_out));
  or or_9 (or_9_out, ~Chip_Select, Reset);  // OR_Gate
  D_Flip_Flop Proc (.clk(CLK), .D(or_4_out), .Q(Proc_q), .reset(or_10_out));  // open: Qn, preset, en
  or or_10 (or_10_out, ~Chip_Select, Reset);  // OR_Gate
  Demultiplexer #(.enable("false")) demultiplexer_2 (
    .out0(Count), .out1(Update_Mem), .in(demultiplexer_3_out0), .sel(Zero_Time));
  Demultiplexer #(.enable("false")) demultiplexer_3 (
    .out0(demultiplexer_3_out0), .out1(Load1), .in(Proc_q), .sel(Changed));
  Clock clock_1 (.out(CLK));
  Comparator #(.width(32)) comparator_2 (.a(register_1_q), .b(Data_In_0), .eq(comparator_2_eq));  // open: gt, lt
  Comparator #(.width(32)) comparator_3 (.a(register_2_q), .b(Data_In_1), .eq(comparator_3_eq));  // open: gt, lt
  Comparator #(.width(32)) comparator_4 (.a(register_3_q), .b(Data_In_2), .eq(comparator_4_eq));  // open: gt, lt
  Comparator #(.width(32)) comparator_5 (.a(register_4_q), .b(Data_In_3), .eq(comparator_5_eq));  // open: gt, lt
  Comparator #(.width(32)) comparator_6 (
    .a(register_5_q), .b({{11{1'b1}}, nRead_Write, Mask, Address}), .eq(comparator_6_eq));  // open: gt, lt
  nand nand_1 (nand_1_out, comparator_6_eq, comparator_2_eq, comparator_3_eq, comparator_4_eq, comparator_5_eq);
  and and_1 (Changed, nand_1_out, Chip_Select);
  or or_11 (Load, Count, Load1, Load0);
  and and_2 (and_2_out, Mask[0], Update_Mem, nRead_Write);
  and and_3 (and_3_out, Mask[1], Update_Mem, nRead_Write);
  and and_4 (and_4_out, Mask[2], Update_Mem, nRead_Write);
  and and_5 (and_5_out, Mask[3], Update_Mem, nRead_Write);
  RAM_part #(.addrWidth(16), .dataWidth(32), .bus("separate")) ram_1 (
    .addr(Address), .din(Data_In_0), .data(Data_Out_0), .str(and_2_out), .sel(Chip_Select), .clk(CLK),
    .ld(and_6_out), .clr(Reset));
  and and_6 (and_6_out, ~nRead_Write, Idle);  // AND_Gate
  RAM_part #(.addrWidth(16), .dataWidth(32), .bus("separate")) ram_2 (
    .addr(Address), .din(Data_In_1), .data(Data_Out_1), .str(and_3_out), .sel(Chip_Select), .clk(CLK),
    .ld(and_7_out), .clr(Reset));
  and and_7 (and_7_out, ~nRead_Write, Idle);  // AND_Gate
  RAM_part #(.addrWidth(16), .dataWidth(32), .bus("separate")) ram_3 (
    .addr(Address), .din(Data_In_2), .data(Data_Out_2), .str(and_4_out), .sel(Chip_Select), .clk(CLK),
    .ld(and_8_out), .clr(Reset));
  and and_8 (and_8_out, ~nRead_Write, Idle);  // AND_Gate
  RAM_part #(.addrWidth(16), .dataWidth(32), .bus("separate")) ram_4 (
    .addr(Address), .din(Data_In_3), .data(Data_Out_3), .str(and_5_out), .sel(Chip_Select), .clk(CLK),
    .ld(and_9_out), .clr(Reset));
  and and_9 (and_9_out, ~nRead_Write, Idle);  // AND_Gate

  assign Read_Time = 4'b0011;
  assign Write_Time = 4'b0010;

  // Other names for the same wires on the sheet: M0 = Mask[0]; M1 = Mask[1]; M2 = Mask[2]; M3 = Mask[3];
  //   RW = nRead_Write; CLR = Reset; CS = Chip_Select; Load2 = Count

  // Notes on the sheet:
  //   NO MODIFICAR
  //   excepto quizás los valores RT y WT
  //   BANK0
  //   BANK1
  //   BANK2
  //   BANK3
endmodule

module S_MIPS (
  input  Kbd_Available,
  input  [6:0] Kbd_ASCII_Data,
  input  [31:0] RAM_Out_0,
  input  [31:0] RAM_Out_1,
  input  Reset,
  input  [31:0] RAM_Out_2,
  input  Clock,
  input  [31:0] RAM_Out_3,
  input  [3:0] Read_Time,
  input  [3:0] Write_Time,
  output Kbd_Enable,
  output [15:0] Address,
  output Kbd_Clear,
  output TTY_Enable,
  output [6:0] TTY_ASCII_Data,
  output Stop,
  output [31:0] RAM_In_0,
  output [31:0] RAM_In_1,
  output [31:0] RAM_In_2,
  output [31:0] RAM_In_3,
  output [3:0] Mask,
  output nRead_Write,
  output Chip_Select
);

  wire enable_inst, Enable_PC, halt, PC_address, r_RAM, read_end, w_RAM;
  wire [31:0] dir_ADDRESS, instuction, write_RAM;

  Control_Unit_2 control_unit_1 (
    .Read_time(Read_Time), .is_halt(halt), .Write_time(Write_Time), .clock(Clock), .Read_RAM(r_RAM),
    .reset(Reset), .Write_RAM(w_RAM), .CS(Chip_Select), .E_inst(enable_inst), .E_PC(Enable_PC),
    .R_W(nRead_Write), .End(Stop), .read_end(read_end), .PC_Address(PC_address));
  Write_to_RAM write_to_ram_1 (
    .dir_ram(dir_ADDRESS), .write_data(write_RAM), .mask(Mask), .RAM_A(Address), .bank_0(RAM_In_0),
    .bank_1(RAM_In_1), .bank_2(RAM_In_2), .bank_3(RAM_In_3));
  Data_Path_2 data_path_1 (
    .address(PC_address), .read_Ram(read_end), .Instruction(instuction), .enable_inst(enable_inst),
    .clock(Clock), .kbd_avail(Kbd_Available), .reset(Reset), .keyboard(Kbd_ASCII_Data),
    .enable_PC(Enable_PC), .TTY_ASCII_Data(TTY_ASCII_Data), .TTY_Enable(TTY_Enable), .Kbd_Enable(Kbd_Enable),
    .write_RAM(write_RAM), .Stop(halt), .w_ram(w_RAM), .r_ram(r_RAM), .dir_address(dir_ADDRESS));
  Read_from_RAM read_from_ram_1 (
    .bank_0(RAM_Out_0), .bank_1(RAM_Out_1), .bank_2(RAM_Out_2), .bank_3(RAM_Out_3), .dir_RAM(dir_ADDRESS),
    .read_data(instuction));

  assign Kbd_Clear = Reset;

  // Other names for the same wires on the sheet: CLK = Clock; CLR = Reset; CS = Chip_Select;
  //   KBD_AVAIL = Kbd_Available; KBD_DATA[6:0] = Kbd_ASCII_Data; RAM_A[15:0] = Address; RAM_INPUT_0[31:0] = RAM_In_0;
  //   RAM_INPUT_1[31:0] = RAM_In_1; RAM_INPUT_2[31:0] = RAM_In_2; RAM_INPUT_3[31:0] = RAM_In_3; RAM_MASK[3:0] = Mask;
  //   RAM_OUTPUT_0[31:0] = RAM_Out_0; RAM_OUTPUT_1[31:0] = RAM_Out_1; RAM_OUTPUT_2[31:0] = RAM_Out_2;
  //   RAM_OUTPUT_3[31:0] = RAM_Out_3; RW = nRead_Write; TTY_DATA[6:0] = TTY_ASCII_Data

  // Notes on the sheet:
  //   RAM ADDRESS
  //   DATA FROM RAM
  //   DATA TO RAM
  //   DATA WRITE MASK
  //   RAM TIMING
  //   RAM CONTROL
  //   KEYBOARD
  //   TTY
  //   SEQUENCING
endmodule

module RAM_Dispatcher (
  input  [3:0] WriteTime,
  input  Clock,
  input  CLR,
  output [31:0] Data,
  output [15:0] Address,
  output [3:0] Mask,
  output Finished,
  output Write
);

  wire demultiplexer_2_out1, demultiplexer_3_out1, End, IDLE_q, IncAddr, Load, or_1_out, or_2_out, While_q,
       WriteEnd;
  wire [3:0] counter_1_q;
  wire [31:0] CurrentAddress_q;

  Counter #(.width(32), .max('hffffffff)) CurrentAddress (
    .count(IncAddr), .Q({CurrentAddress_q[31:18], Address, CurrentAddress_q[1:0]}), .clk(Clock), .clr(CLR));  // open: load, D, carry
  or or_1 (or_1_out, IncAddr, demultiplexer_3_out1, Finished);
  D_Flip_Flop IDLE (.clk(Clock), .D(or_1_out), .Q(IDLE_q), .preset(CLR));  // open: Qn, en, reset
  Demultiplexer #(.enable("false")) demultiplexer_1 (.out0(Load), .out1(Finished), .in(IDLE_q), .sel(End));
  D_Flip_Flop While (.clk(Clock), .D(or_2_out), .Q(While_q), .reset(CLR));  // open: Qn, preset, en
  or or_2 (or_2_out, Write, Load);
  RAM_part #(.addrWidth(18), .dataWidth(32)) ram_1 (
    .addr({Address, CurrentAddress_q[1:0]}), .data(Data), .clk(Clock));  // open: sel, ld, clr
  Demultiplexer #(.enable("false")) demultiplexer_2 (
    .out0(Write), .out1(demultiplexer_2_out1), .in(While_q), .sel(WriteEnd));
  Decoder #(.select(2)) decoder_1 (
    .out0(Mask[0]), .out1(Mask[1]), .out2(Mask[2]), .out3(Mask[3]), .sel(CurrentAddress_q[1:0]));  // open: en
  Demultiplexer #(.enable("false")) demultiplexer_3 (
    .out0(IncAddr), .out1(demultiplexer_3_out1), .in(demultiplexer_2_out1), .sel(End));
  Counter #(.width(4), .max('hf)) counter_1 (
    .load(Load), .D(WriteTime), .count(Write), .Q(counter_1_q), .clk(Clock));  // open: carry, clr
  Comparator #(.width(32)) comparator_1 (.a(Data), .b({32{1'b1}}), .eq(End));  // open: gt, lt
  Comparator #(.width(4)) comparator_2 (.a(4'b0000), .b(counter_1_q), .eq(WriteEnd));  // open: gt, lt

  // Other names for the same wires on the sheet: CLK = Clock; Count = Write; WT[3:0] = WriteTime
endmodule

module Control_Unit_2 (
  input  [3:0] Read_time,
  input  is_halt,
  input  [3:0] Write_time,
  input  clock,
  input  Read_RAM,
  input  reset,
  input  Write_RAM,
  output CS,
  output E_inst,
  output E_PC,
  output R_W,
  output End,
  output read_end,
  output PC_Address
);

  wire c1, c2, demultiplexer_1_out0, demultiplexer_2_out1, demultiplexer_3_out0, demultiplexer_4_out0,
       demultiplexer_4_out1, demultiplexer_5_out0, Excute_q, Idle_q, or_2_out, or_3_out, or_5_out, or_8_out,
       R_W_t, RAM, RAM_read_load, rst_1, timer_1_out_4, timer_2_out_4;
  wire [3:0] multiplexer_1_out;

  or or_1 (E_PC, demultiplexer_5_out0, RAM_read_load);
  or or_2 (or_2_out, demultiplexer_1_out0, R_W_t);
  or or_3 (or_3_out, demultiplexer_5_out0, RAM_read_load, demultiplexer_2_out1);
  D_Flip_Flop d_ff_1 (.clk(clock), .D(or_2_out), .Q(c2), .reset(reset));  // open: Qn, preset, en
  Multiplexer #(.width(4), .enable("false")) multiplexer_1 (
    .in0(Read_time), .in1(Write_time), .out(multiplexer_1_out), .sel(Write_RAM));
  D_Flip_Flop Idle (.clk(clock), .D(or_3_out), .Q(Idle_q), .preset(reset));  // open: Qn, en, reset
  Demultiplexer #(.enable("false")) demultiplexer_1 (
    .out0(demultiplexer_1_out0), .out1(read_end), .in(c2), .sel(timer_1_out_4));
  Timer timer_1 (.Time(multiplexer_1_out), .Clock(clock), .Reset(R_W_t), .out_4(timer_1_out_4));
  or or_4 (RAM, Read_RAM, Write_RAM);
  Demultiplexer #(.enable("false")) demultiplexer_2 (
    .out0(rst_1), .out1(demultiplexer_2_out1), .in(Idle_q), .sel(reset));
  D_Flip_Flop d_ff_2 (.clk(clock), .D(read_end), .Q(RAM_read_load), .reset(reset));  // open: Qn, preset, en
  or or_5 (or_5_out, demultiplexer_3_out0, rst_1);
  D_Flip_Flop Inst (.clk(clock), .D(or_5_out), .Q(c1), .reset(reset));  // open: Qn, preset, en
  Demultiplexer #(.enable("false")) demultiplexer_3 (
    .out0(demultiplexer_3_out0), .out1(E_inst), .in(c1), .sel(timer_2_out_4));
  Timer timer_2 (.Time(Read_time), .Clock(clock), .Reset(rst_1), .out_4(timer_2_out_4));
  or or_6 (CS, c1, c2);
  and and_1 (R_W, c2, Write_RAM);
  or or_7 (PC_Address, c1, rst_1, E_PC);
  D_Flip_Flop Excute (.clk(clock), .D(E_inst), .Q(Excute_q), .reset(reset));  // open: Qn, preset, en
  Demultiplexer #(.enable("false")) demultiplexer_4 (
    .out0(demultiplexer_4_out0), .out1(demultiplexer_4_out1), .in(Excute_q), .sel(is_halt));
  Demultiplexer #(.enable("false")) demultiplexer_5 (
    .out0(demultiplexer_5_out0), .out1(R_W_t), .in(demultiplexer_4_out0), .sel(RAM));
  or or_8 (or_8_out, demultiplexer_4_out1, End);
  D_Flip_Flop u_End (.clk(clock), .D(or_8_out), .Q(End), .reset(reset));  // open: Qn, preset, en

  // Other names for the same wires on the sheet: clk = clock; halt = is_halt; rst = reset; rst_2 = R_W_t

  // Notes on the sheet:
  //   Inputs
  //   CONTROL UNIT
  //   Outputs
endmodule

module Timer (
  input  [3:0] Time,
  input  Clock,
  input  Reset,
  output out_4
);

  wire [3:0] counter_1_q;

  Counter #(.width(4), .max('hf)) counter_1 (
    .count(1'b1), .Q(counter_1_q), .clk(Clock), .clr(Reset));  // open: load, D, carry
  Comparator #(.width(4)) comparator_1 (.a(Time), .b(counter_1_q), .eq(out_4));  // open: gt, lt

  // Notes on the sheet:
  //   Input
  //   TIMER
  //   Output
endmodule

module Data_Path_2 (
  input  address,
  input  read_Ram,
  input  [31:0] Instruction,
  input  enable_inst,
  input  clock,
  input  kbd_avail,
  input  reset,
  input  [6:0] keyboard,
  input  enable_PC,
  output [6:0] TTY_ASCII_Data,
  output TTY_Enable,
  output Kbd_Enable,
  output [31:0] write_RAM,
  output Stop,
  output w_ram,
  output r_ram,
  output [31:0] dir_address
);

  wire ALU_type_i, beq, bgtz, blez, bltz, bne, is_ALU, is_HL, is_negative, is_zero, j, jr, lw, mfhi, mflo,
       nop, oRF, pop, push, r_w, rnd, sw, tty, type_i;
  wire [3:0] ALU_selct;
  wire [4:0] multiplexer_1_out, Rd, Rs, Rt, x;
  wire [5:0] instruction_separator_1_func_code, instruction_separator_1_output_2;
  wire [15:0] constat;
  wire [25:0] jump;
  wire [31:0] ALU_Output, bit_extender_1_out, branch_control_1_output, High, high_t, Low, multiplexer_2_out,
       multiplexer_3_out, Output_A, Output_B, PC, register_1_q, register_file_input_1_rf_input, SP;

  Register #(.width(32)) register_1 (.D(Instruction), .en(enable_inst), .Q(register_1_q), .clk(clock), .clr(reset));
  Instruction_Separator instruction_separator_1 (
    .Instruction(register_1_q), .func_code(instruction_separator_1_func_code), .Rt(Rt), .x(x), .Rs(Rs),
    .Rd(Rd), .Output(jump), .constat(constat), .Output_2(instruction_separator_1_output_2));
  Branch_Control branch_control_1 (
    .PC(PC), .Rs(Output_A), .Rt(Output_B), .Constat(constat), .Jump(jump), .beq(beq), .bne(bne), .blez(blez),
    .bgtz(bgtz), .bltz(bltz), .j(j), .jr(jr), .Output(branch_control_1_output));
  Program_Counter program_counter_1 (
    .in_1(branch_control_1_output), .Output(PC), .Enable(enable_PC), .Clock(clock), .Reset(reset));
  Instruction_Decoder instruction_decoder_1 (
    .op_code(instruction_separator_1_output_2), .func_code(instruction_separator_1_func_code), .mfhi(mfhi),
    .halt(Stop), .pop(pop), .bne(bne), .is_LH(is_HL), .lw(lw), .mflo(mflo), .tty(tty), .push(push),
    .blez(blez), .type_i(type_i), .sw(sw), .nop(nop), .rnd(rnd), .j(j), .bgtz(bgtz), .is_ALU(is_ALU),
    .ALU_selector(ALU_selct), .jr(jr), .kbd(Kbd_Enable), .beq(beq), .bltz(bltz), .ALU_type_i(ALU_type_i));
  Dir_RAM dir_ram_1 (
    .sw(sw), .ALU_Output(ALU_Output), .lw(lw), .pop(pop), .SP(SP), .push(push), .PC_Addr(address), .PC(PC),
    .Rs(Output_A), .Rt(Output_B), .Dir_RAM(dir_address), .Write_RAM(w_ram), .Read_RAM(r_ram),
    .RAM_w(write_RAM), .tty_data(TTY_ASCII_Data));
  R_W r_w_1 (.ORF(oRF), .Is_ALU(is_ALU), .PC(enable_PC), .Read_RAM(read_Ram), .Pop(pop), .LW(lw), .R_W(r_w));
  Register_File_Input register_file_input_1 (
    .rnd(rnd), .High(high_t), .kbd(Kbd_Enable), .Low(Low), .mflo(mflo), .pop(pop), .RAM(Instruction),
    .lw(lw), .Kbd_Avail(kbd_avail), .ALU_Output(ALU_Output), .clk(clock), .Keyboard(keyboard),
    .RF_Input(register_file_input_1_rf_input), .mfhi(mfhi), .ORF(oRF));
  and and_1 (TTY_Enable, enable_PC, tty);
  Multiplexer #(.width(5), .enable("false")) multiplexer_1 (.in0(Rd), .in1(Rt), .out(multiplexer_1_out), .sel(type_i));
  // Probe on multiplexer_2_out
  Register_File_2 register_file_1 (
    .Data_Adress(multiplexer_1_out), .Data_Input(register_file_input_1_rf_input), .Selector_A(Rs),
    .Selector_B(Rt), .R_W(r_w), .Clock(clock), .Reset(reset), .High(High), .Enable_HIgh_Low(is_HL),
    .Enable_PC(enable_PC), .Pop(pop), .Push(push), .Output_A(Output_A), .Output_B(Output_B), .SP(SP),
    .Low(Low), .High_2(high_t));
  // Probe on multiplexer_3_out
  Multiplexer #(.width(32), .enable("false")) multiplexer_2 (
    .in0(Output_B), .in1(multiplexer_3_out), .out(multiplexer_2_out), .sel(type_i));
  ALU_2 alu_1 (
    .A(Output_A), .B(multiplexer_2_out), .Selector(ALU_selct), .Output(ALU_Output), .High_Output(High),
    .Is_Zero(is_zero), .Is_Negative(is_negative));
  Multiplexer #(.width(32), .enable("false")) multiplexer_3 (
    .in0(bit_extender_1_out), .in1({{16{1'b0}}, constat}), .out(multiplexer_3_out), .sel(ALU_type_i));
  // Probe on {{16{1'b0}}, constat}
  assign bit_extender_1_out = {{16{constat[15]}}, constat};  // Bit_Extender bit_extender_1
  // Probe on bit_extender_1_out

  // Other names for the same wires on the sheet: clk = clock; halt = Stop; kbd = Kbd_Enable; rst = reset;
  //   TTY_DATA[6:0] = TTY_ASCII_Data

  // Notes on the sheet:
  //   Input
  //   DATA PATH
  //   Output
endmodule

module Branch_Control (
  input  [31:0] PC,
  input  [31:0] Rs,
  input  [31:0] Rt,
  input  [15:0] Constat,
  input  [25:0] Jump,
  input  beq,
  input  bne,
  input  blez,
  input  bgtz,
  input  bltz,
  input  j,
  input  jr,
  output [31:0] Output
);

  wire _0, _0_t, and_1_out, and_2_out, and_3_out, and_4_out, and_5_out, b, not_1_out, not_2_out, or_1_out,
       tunnel;
  wire [1:0] selector;
  wire [31:0] PC___4, PC___4___4_offset;
  wire [31:18] _4_offset;

  Comparator #(.width(32)) comparator_1 (.a(Rs), .b(Rt), .eq(tunnel));  // open: gt, lt
  Comparator #(.width(32)) comparator_2 (.a(Rs), .b({32{1'b0}}), .eq(_0_t), .lt(_0));  // open: gt
  assign _4_offset = {{13{Constat[15]}}, Constat[15]};  // Bit_Extender bit_extender_1
  not not_1 (not_1_out, tunnel);
  or or_1 (or_1_out, _0_t, _0);
  not not_2 (not_2_out, or_1_out);
  // Probe on {_4_offset, Constat, 2'b00}
  and and_1 (and_1_out, beq, tunnel);
  and and_2 (and_2_out, bne, not_1_out);
  and and_3 (and_3_out, blez, or_1_out);
  and and_4 (and_4_out, not_2_out, bgtz);
  and and_5 (and_5_out, bltz, _0);
  or or_2 (b, and_1_out, and_2_out, and_3_out, and_4_out, and_5_out);
  Adder #(.width(32)) adder_1 (.a(PC), .b(32'h4), .out(PC___4));  // open: cin, cout
  Adder #(.width(32)) adder_2 (
    .a(PC___4), .b({_4_offset, Constat, 2'b00}), .out(PC___4___4_offset));  // open: cin, cout
  // Probe on PC___4
  or or_3 (selector[0], b, j);
  or or_4 (selector[1], jr, j);
  Multiplexer #(.select(2), .width(32), .enable("false")) multiplexer_1 (
    .in0(PC___4), .in1(PC___4___4_offset), .in2(Rs), .in3({PC[31:28], Jump, 2'b00}), .out(Output),
    .sel(selector));
  // Probe on selector

  // Other names for the same wires on the sheet: _4_offset[17:2] = Constat; destiny_j[31:2] = {PC[31:28], Jump};
  //   instruction[31:0] = Output

  // Notes on the sheet:
  //   Input
  //   BRANCH CONTROL
  //   Output
endmodule

module Program_Counter (
  input  [31:0] in_1,
  input  Clock,
  input  Reset,
  input  Enable,
  output [31:0] Output
);

  Register #(.width(32)) register_1 (.D(in_1), .en(Enable), .Q(Output), .clk(Clock), .clr(Reset));

  // Notes on the sheet:
  //   Input
  //   PROGRAM COUNTER
endmodule

module Dir_RAM (
  input  sw,
  input  [31:0] ALU_Output,
  input  lw,
  input  pop,
  input  [31:0] SP,
  input  push,
  input  PC_Addr,
  input  [31:0] PC,
  input  [31:0] Rs,
  input  [31:0] Rt,
  output [31:0] Dir_RAM,
  output Write_RAM,
  output Read_RAM,
  output [31:0] RAM_w,
  output [6:0] tty_data
);

  wire [1:0] Selector;
  wire [31:0] multiplexer_1_out, subtractor_1_out;

  or or_1 (Selector[1], pop, PC_Addr, push);
  or or_2 (Selector[0], sw, PC_Addr, lw);
  Subtractor #(.width(32)) subtractor_1 (.a(SP), .b(32'h4), .out(subtractor_1_out));  // open: bin, bout
  or or_3 (Write_RAM, sw, push);
  Multiplexer #(.width(32), .enable("false")) multiplexer_1 (
    .in0(SP), .in1(subtractor_1_out), .out(multiplexer_1_out), .sel(push));
  Multiplexer #(.select(2), .width(32), .enable("false")) multiplexer_2 (
    .in0(PC), .in1(ALU_Output), .in2(multiplexer_1_out), .in3(PC), .out(Dir_RAM), .sel(Selector));
  or or_4 (Read_RAM, lw, pop);
  Multiplexer #(.width(32), .enable("false")) multiplexer_3 (.in0(Rs), .in1(Rt), .out(RAM_w), .sel(sw));

  assign tty_data = Rs[6:0];

  // Other names for the same wires on the sheet: ALU[31:0] = ALU_Output

  // Notes on the sheet:
  //   Inputs
  //   DIR RAM
  //   Outputs
endmodule

module R_W (
  input  ORF,
  input  Is_ALU,
  input  PC,
  input  Read_RAM,
  input  Pop,
  input  LW,
  output R_W
);

  wire and_1_out, and_2_out, or_1_out, or_2_out;

  or or_1 (or_1_out, ORF, Is_ALU);
  or or_2 (or_2_out, LW, Pop);
  and and_1 (and_1_out, PC, or_1_out);
  and and_2 (and_2_out, or_2_out, Read_RAM);
  or or_3 (R_W, and_1_out, and_2_out);

  // Other names for the same wires on the sheet: ALU = Is_ALU

  // Notes on the sheet:
  //   Inputs
  //   R/W
  //   Output
endmodule

module Register_File_2 (
  input  [4:0] Data_Adress,
  input  [31:0] Data_Input,
  input  [4:0] Selector_A,
  input  [4:0] Selector_B,
  input  R_W,
  input  Clock,
  input  Reset,
  input  [31:0] High,
  input  Enable_HIgh_Low,
  input  Enable_PC,
  input  Pop,
  input  Push,
  output [31:0] Output_A,
  output [31:0] Output_B,
  output [31:0] SP,
  output [31:0] Low,
  output [31:0] High_2
);

  wire and_1_out, E_SP, Input_0, Input_1, Input_2, Input_3, Input_4, Input_5, Input_6, Input_7, Input_8,
       Input_9, Input_10, Input_11, Input_12, Input_13, Input_14, Input_15, Input_16, Input_17, Input_18,
       Input_19, Input_20, Input_21, Input_22, Input_23, Input_24, Input_25, Input_26, Input_27, Input_28,
       Input_29, Input_30, Input_31, or_1_out;
  wire [31:0] multiplexer_1_out, Output_0, Output_1, Output_2, Output_3, Output_4, Output_5, Output_6,
       Output_7, Output_8, Output_9, Output_10, Output_11, Output_12, Output_13, Output_14, Output_15,
       Output_16, Output_17, Output_18, Output_19, Output_20, Output_21, Output_22, Output_23, Output_24,
       Output_25, Output_26, Output_27, Output_28, Output_29, Output_30, Output_31, SP___4, SP___4_t,
       SP_Input;

  Demultiplexer #(.select(5), .enable("false")) demultiplexer_1 (
    .out0(Input_0), .out1(Input_1), .out2(Input_2), .out3(Input_3), .out4(Input_4), .out5(Input_5),
    .out6(Input_6), .out7(Input_7), .out8(Input_8), .out9(Input_9), .out10(Input_10), .out11(Input_11),
    .out12(Input_12), .out13(Input_13), .out14(Input_14), .out15(Input_15), .out16(Input_16),
    .out17(Input_17), .out18(Input_18), .out19(Input_19), .out20(Input_20), .out21(Input_21),
    .out22(Input_22), .out23(Input_23), .out24(Input_24), .out25(Input_25), .out26(Input_26),
    .out27(Input_27), .out28(Input_28), .out29(Input_29), .out30(Input_30), .out31(Input_31), .in(R_W),
    .sel(Data_Adress));
  Register #(.width(32)) R00 (.D({32{1'b0}}), .en(Input_0), .Q(Output_0), .clk(Clock), .clr(Reset));
  Register #(.width(32)) R04 (.D(Data_Input), .en(Input_4), .Q(Output_4), .clk(Clock), .clr(Reset));
  Register #(.width(32)) R08 (.D(Data_Input), .en(Input_8), .Q(Output_8), .clk(Clock), .clr(Reset));
  Register #(.width(32)) R12 (.D(Data_Input), .en(Input_12), .Q(Output_12), .clk(Clock), .clr(Reset));
  Register #(.width(32)) R16 (.D(Data_Input), .en(Input_16), .Q(Output_16), .clk(Clock), .clr(Reset));
  Register #(.width(32)) R20 (.D(Data_Input), .en(Input_20), .Q(Output_20), .clk(Clock), .clr(Reset));
  Register #(.width(32)) R24 (.D(Data_Input), .en(Input_24), .Q(Output_24), .clk(Clock), .clr(Reset));
  Register #(.width(32)) R28 (.D(Data_Input), .en(Input_28), .Q(Output_28), .clk(Clock), .clr(Reset));
  Register #(.width(32)) R01 (.D(Data_Input), .en(Input_1), .Q(Output_1), .clk(Clock), .clr(Reset));
  Register #(.width(32)) R05 (.D(Data_Input), .en(Input_5), .Q(Output_5), .clk(Clock), .clr(Reset));
  Register #(.width(32)) R09 (.D(Data_Input), .en(Input_9), .Q(Output_9), .clk(Clock), .clr(Reset));
  Register #(.width(32)) R13 (.D(Data_Input), .en(Input_13), .Q(Output_13), .clk(Clock), .clr(Reset));
  Register #(.width(32)) R17 (.D(Data_Input), .en(Input_17), .Q(Output_17), .clk(Clock), .clr(Reset));
  Register #(.width(32)) R21 (.D(Data_Input), .en(Input_21), .Q(Output_21), .clk(Clock), .clr(Reset));
  Register #(.width(32)) R25 (.D(Data_Input), .en(Input_25), .Q(Output_25), .clk(Clock), .clr(Reset));
  Register #(.width(32)) R29 (.D(Data_Input), .en(Input_29), .Q(Output_29), .clk(Clock), .clr(Reset));
  Register #(.width(32)) R02 (.D(Data_Input), .en(Input_2), .Q(Output_2), .clk(Clock), .clr(Reset));
  Register #(.width(32)) R06 (.D(Data_Input), .en(Input_6), .Q(Output_6), .clk(Clock), .clr(Reset));
  Register #(.width(32)) R10 (.D(Data_Input), .en(Input_10), .Q(Output_10), .clk(Clock), .clr(Reset));
  Register #(.width(32)) R14 (.D(Data_Input), .en(Input_14), .Q(Output_14), .clk(Clock), .clr(Reset));
  Register #(.width(32)) R18 (.D(Data_Input), .en(Input_18), .Q(Output_18), .clk(Clock), .clr(Reset));
  Register #(.width(32)) R22 (.D(Data_Input), .en(Input_22), .Q(Output_22), .clk(Clock), .clr(Reset));
  Register #(.width(32)) R26 (.D(Data_Input), .en(Input_26), .Q(Output_26), .clk(Clock), .clr(Reset));
  Register #(.width(32)) R30 (.D(Data_Input), .en(Input_30), .Q(Output_30), .clk(Clock), .clr(Reset));
  Register #(.width(32)) u_High (.D(High), .en(Enable_HIgh_Low), .Q(High_2), .clk(Clock), .clr(Reset));
  Adder #(.width(32)) adder_1 (.a(32'h4), .b(SP), .out(SP___4));  // open: cin, cout
  Multiplexer #(.width(32), .enable("false")) multiplexer_1 (
    .in0(SP___4), .in1(SP___4_t), .out(multiplexer_1_out), .sel(Push));
  Multiplexer #(.width(32), .enable("false")) multiplexer_2 (
    .in0(multiplexer_1_out), .in1(Data_Input), .out(SP_Input), .sel(Input_31));
  Register #(.width(32)) R03 (.D(Data_Input), .en(Input_3), .Q(Output_3), .clk(Clock), .clr(Reset));
  Register #(.width(32)) R07 (.D(Data_Input), .en(Input_7), .Q(Output_7), .clk(Clock), .clr(Reset));
  Register #(.width(32)) R11 (.D(Data_Input), .en(Input_11), .Q(Output_11), .clk(Clock), .clr(Reset));
  Register #(.width(32)) R15 (.D(Data_Input), .en(Input_15), .Q(Output_15), .clk(Clock), .clr(Reset));
  Register #(.width(32)) R19 (.D(Data_Input), .en(Input_19), .Q(Output_19), .clk(Clock), .clr(Reset));
  Register #(.width(32)) R23 (.D(Data_Input), .en(Input_23), .Q(Output_23), .clk(Clock), .clr(Reset));
  Register #(.width(32)) R27 (.D(Data_Input), .en(Input_27), .Q(Output_27), .clk(Clock), .clr(Reset));
  Register #(.width(32)) u_Low (.D(Data_Input), .en(Enable_HIgh_Low), .Q(Low), .clk(Clock), .clr(Reset));
  Subtractor #(.width(32)) subtractor_1 (.a(SP), .b(32'h4), .out(SP___4_t));  // open: bin, bout
  or or_1 (or_1_out, Push, Pop);
  Register #(.width(32)) u_SP (.D(SP_Input), .en(E_SP), .Q(SP), .clk(Clock), .clr(Reset));
  and and_1 (and_1_out, or_1_out, Enable_PC);
  or or_2 (E_SP, Reset, and_1_out, Input_31);
  Multiplexer #(.select(5), .width(32), .enable("false")) multiplexer_3 (
    .in0(Output_0), .in1(Output_1), .in2(Output_2), .in3(Output_3), .in4(Output_4), .in5(Output_5),
    .in6(Output_6), .in7(Output_7), .in8(Output_8), .in9(Output_9), .in10(Output_10), .in11(Output_11),
    .in12(Output_12), .in13(Output_13), .in14(Output_14), .in15(Output_15), .in16(Output_16),
    .in17(Output_17), .in18(Output_18), .in19(Output_19), .in20(Output_20), .in21(Output_21),
    .in22(Output_22), .in23(Output_23), .in24(Output_24), .in25(Output_25), .in26(Output_26),
    .in27(Output_27), .in28(Output_28), .in29(Output_29), .in30(Output_30), .in31(Output_31), .out(Output_A),
    .sel(Selector_A));
  Multiplexer #(.select(5), .width(32), .enable("false")) multiplexer_4 (
    .in0(Output_0), .in1(Output_1), .in2(Output_2), .in3(Output_3), .in4(Output_4), .in5(Output_5),
    .in6(Output_6), .in7(Output_7), .in8(Output_8), .in9(Output_9), .in10(Output_10), .in11(Output_11),
    .in12(Output_12), .in13(Output_13), .in14(Output_14), .in15(Output_15), .in16(Output_16),
    .in17(Output_17), .in18(Output_18), .in19(Output_19), .in20(Output_20), .in21(Output_21),
    .in22(Output_22), .in23(Output_23), .in24(Output_24), .in25(Output_25), .in26(Output_26),
    .in27(Output_27), .in28(Output_28), .in29(Output_29), .in30(Output_30), .in31(Output_31), .out(Output_B),
    .sel(Selector_B));

  // Other names for the same wires on the sheet: Clk = Clock; Data_Address[4:0] = Data_Adress; E_HL = Enable_HIgh_Low;
  //   E_PC = Enable_PC; High_Input[31:0] = High; High_t[31:0] = High_2; Rst = Reset

  // Notes on the sheet:
  //   Inputs
  //   REGISTER FILE
  //   Outputs
endmodule

module Register_File_Input (
  input  rnd,
  input  [31:0] High,
  input  kbd,
  input  mfhi,
  input  [31:0] Low,
  input  mflo,
  input  pop,
  input  [31:0] RAM,
  input  lw,
  input  Kbd_Avail,
  input  [31:0] ALU_Output,
  input  clk,
  input  [6:0] Keyboard,
  output [31:0] RF_Input,
  output ORF
);

  wire ram_t;
  wire [2:0] selector;
  wire [31:0] KBD_Input, random;

  Multiplexer #(.width(32), .enable("false")) multiplexer_1 (
    .in0({32{1'b1}}), .in1({{25{1'b0}}, Keyboard}), .out(KBD_Input), .sel(Kbd_Avail));
  or or_1 (ram_t, pop, lw);
  Random #(.width(32)) random_1 (.clk(clk), .next(rnd), .out(random));  // open: clr
  or or_2 (selector[0], rnd, kbd, mfhi);
  or or_3 (selector[1], ram_t, mflo);
  or or_4 (selector[2], rnd, ram_t);
  // Probe on selector
  Multiplexer #(.select(3), .width(32), .enable("false")) multiplexer_2 (
    .in0(ALU_Output), .in1(High), .in2(Low), .in3(RAM), .in4(KBD_Input), .in5(random), .out(RF_Input),
    .sel(selector));  // open: in6, in7
  or or_5 (ORF, rnd, kbd, mfhi, mflo);

  // Other names for the same wires on the sheet: ALU[31:0] = ALU_Output; Keyboard_t[6:0] = Keyboard

  // Notes on the sheet:
  //   Inputs
  //   Output
endmodule

module Signed_Multiplier (
  input  [31:0] A,
  input  [31:0] B,
  output [31:0] Low,
  output [31:0] High
);

  wire Selector;
  wire [31:0] multiplexer_1_out, multiplexer_2_out, multiplier_1_out, negator_1_out, negator_2_out,
       negator_3_out;

  // Probe on A
  // Probe on B
  xor xor_1 (Selector, A[31], B[31]);
  Negator #(.width(32)) negator_1 (.in(A), .out(negator_1_out));
  Negator #(.width(32)) negator_2 (.in(B), .out(negator_2_out));
  Multiplexer #(.width(32)) multiplexer_1 (
    .in0(A), .in1(negator_1_out), .out(multiplexer_1_out), .sel(A[31]));  // open: en
  Multiplexer #(.width(32)) multiplexer_2 (
    .in0(B), .in1(negator_2_out), .out(multiplexer_2_out), .sel(B[31]));  // open: en
  Multiplier #(.width(32)) multiplier_1 (
    .a(multiplexer_1_out), .b(multiplexer_2_out), .out(multiplier_1_out), .cout(High));  // open: cin
  Negator #(.width(32)) negator_3 (.in(multiplier_1_out), .out(negator_3_out));
  Multiplexer #(.width(32)) multiplexer_3 (
    .in0(multiplier_1_out), .in1(negator_3_out), .out(Low), .sel(Selector));  // open: en
  // Probe on Low
  // Probe on High

  // Other names for the same wires on the sheet: Selector_A = A[31]; Selector_B = B[31]

  // Notes on the sheet:
  //   Input
  //   SIGNED MULTIPLIER
  //   Output
endmodule

module Signed_Divider (
  input  [31:0] A,
  input  [31:0] B,
  output [31:0] Low,
  output [31:0] High
);

  wire Selector, Selector_t;
  wire [31:0] divider_1_out, divider_1_rem, multiplexer_1_out, multiplexer_2_out, negator_1_out,
       negator_2_out, negator_3_out, negator_4_out;

  // Probe on A
  // Probe on B
  Negator #(.width(32)) negator_1 (.in(A), .out(negator_1_out));
  Negator #(.width(32)) negator_2 (.in(B), .out(negator_2_out));
  xor xor_1 (Selector, A[31], B[31]);
  Multiplexer #(.width(32), .enable("false")) multiplexer_1 (
    .in0(A), .in1(negator_1_out), .out(multiplexer_1_out), .sel(A[31]));
  Multiplexer #(.width(32), .enable("false")) multiplexer_2 (
    .in0(B), .in1(negator_2_out), .out(multiplexer_2_out), .sel(B[31]));
  Divider #(.width(32)) divider_1 (
    .a(multiplexer_1_out), .b(multiplexer_2_out), .out(divider_1_out), .rem(divider_1_rem));  // open: upper
  Negator #(.width(32)) negator_3 (.in(divider_1_out), .out(negator_3_out));
  Negator #(.width(32)) negator_4 (.in(divider_1_rem), .out(negator_4_out));
  // Probe on Low
  Multiplexer #(.width(32), .enable("false")) multiplexer_3 (
    .in0(divider_1_out), .in1(negator_3_out), .out(Low), .sel(Selector_t));
  Multiplexer #(.width(32), .enable("false")) multiplexer_4 (
    .in0(divider_1_rem), .in1(negator_4_out), .out(High), .sel(A[31]));
  // Probe on High

  // Other names for the same wires on the sheet: Selector_A = A[31]; Selector_B = B[31]

  // Notes on the sheet:
  //   Input
  //   SIGNED DIVIDER
  //   Output
endmodule

// or
module ALU_Encoder (
  input  add,
  input  addi,
  input  sub,
  input  slt,
  input  slti,
  input  sltu,
  input  sltui,
  input  \and ,
  input  andi,
  input  \or ,
  input  ori,
  input  \xor ,
  input  xori,
  input  \nor ,
  input  mult,
  input  mulu,
  input  div,
  input  divu,
  output [3:0] Selector
);

  wire add_t, and_t, or_t, slt_t, sltu_t, xor_t;

  or or_1 (add_t, add, addi);
  or or_2 (slt_t, slt, slti);
  or or_3 (sltu_t, sltu, sltui);
  or or_4 (and_t, \and , andi);
  or or_5 (or_t, \or , ori);
  or or_6 (xor_t, \xor , xori);
  or or_7 (Selector[0], sub, sltu_t, or_t, \nor , mulu, divu);
  or or_8 (Selector[1], slt_t, sltu_t, xor_t, \nor , div, divu);
  or or_9 (Selector[2], and_t, or_t, xor_t, \nor );
  or or_10 (Selector[3], mult, mulu, div, divu);

  // Other names for the same wires on the sheet: bit_0 = Selector[0]; bit_1 = Selector[1]; bit_2 = Selector[2];
  //   bit_3 = Selector[3]

  // Notes on the sheet:
  //   Input
  //   ALU ENCODER
  //   Output
endmodule

module ALU_2 (
  input  [31:0] A,
  input  [31:0] B,
  input  [3:0] Selector,
  output [31:0] Output,
  output [31:0] High_Output,
  output Is_Zero,
  output Is_Negative
);

  wire comparator_1_lt, comparator_2_lt;
  wire [31:0] add, \and , div_H, div_L, divu_H, divu_L, high, mult_H, mult_L, mulu_H, mulu_L, \nor , \or ,
       slt, sltu, sub, \xor ;

  Adder #(.width(32)) adder_1 (.a(A), .b(B), .out(add));  // open: cin, cout
  Subtractor #(.width(32)) subtractor_1 (.a(A), .b(B), .out(sub));  // open: bin, bout
  Comparator #(.width(32)) comparator_1 (.a(A), .b(B), .lt(comparator_1_lt));  // open: gt, eq
  Comparator #(.width(32)) comparator_2 (.a(A), .b(B), .lt(comparator_2_lt));  // open: gt, eq
  assign slt = {{31{1'b0}}, comparator_1_lt};  // Bit_Extender bit_extender_1
  assign sltu = {{31{1'b0}}, comparator_2_lt};  // Bit_Extender bit_extender_2
  assign \and  = A & B;  // AND_Gate and_1, 32 bits wide
  assign \or  = A | B;  // OR_Gate or_1, 32 bits wide
  Multiplexer #(.select(4), .width(32), .enable("false")) multiplexer_1 (
    .in0(add), .in1(sub), .in2(slt), .in3(sltu), .in4(\and ), .in5(\or ), .in6(\xor ), .in7(\nor ),
    .in8(mult_L), .in9(mulu_L), .in10(div_L), .in11(divu_L), .in12({32{1'b0}}), .in13({32{1'b0}}),
    .in14({32{1'b0}}), .in15({32{1'b0}}), .out(Output), .sel(Selector));
  assign \xor  = A ^ B;  // XOR_Gate xor_1, 32 bits wide
  assign \nor  = ~(A | B);  // NOR_Gate nor_1, 32 bits wide
  Multiplexer #(.select(2), .width(32), .enable("false")) multiplexer_2 (
    .in0(mult_H), .in1(mulu_H), .in2(div_H), .in3(divu_H), .out(high), .sel(Selector[1:0]));
  Multiplexer #(.width(32), .enable("false")) multiplexer_3 (
    .in0({32{1'b0}}), .in1(high), .out(High_Output), .sel(Selector[3]));
  Signed_Multiplier signed_multiplier_1 (.A(A), .B(B), .Low(mult_L), .High(mult_H));
  Multiplier #(.width(32)) multiplier_1 (.a(A), .b(B), .out(mulu_L), .cout(mulu_H));  // open: cin
  Signed_Divider signed_divider_1 (.A(A), .B(B), .Low(div_L), .High(div_H));
  Divider #(.width(32)) divider_1 (.a(A), .b(B), .out(divu_L), .rem(divu_H));  // open: upper
  // Probe on mult_H
  Comparator #(.width(32)) comparator_3 (.a(Output), .b({32{1'b0}}), .eq(Is_Zero), .lt(Is_Negative));  // open: gt

  // Other names for the same wires on the sheet: High_Selector[1:0] = Selector[1:0]; Select_High_Output = Selector[3]

  // Notes on the sheet:
  //   Input
  //   0000
  //   0001
  //   0010
  //   0011
  //   0100
  //   0101
  //   ALUcinante
  //   0110
  //   0111
  //   1000
  //   1001
  //   1010
  //   1011
  //   Output
endmodule

module Instruction_Separator (
  input  [31:0] Instruction,
  output [5:0] func_code,
  output [4:0] Rt,
  output [4:0] x,
  output [4:0] Rs,
  output [4:0] Rd,
  output [25:0] Output,
  output [15:0] constat,
  output [5:0] Output_2
);


  assign constat = Instruction[15:0];
  assign func_code = Instruction[5:0];
  assign Output = Instruction[25:0];
  assign Output_2 = Instruction[31:26];
  assign Rd = Instruction[15:11];
  assign Rs = Instruction[25:21];
  assign Rt = Instruction[20:16];
  assign x = Instruction[10:6];

  // Other names for the same wires on the sheet: jump[25:0] = Instruction[25:0]; op_code[5:0] = Instruction[31:26]

  // Notes on the sheet:
  //   Input
  //   INSTRUCTION SEPARATOR
  //   Output
endmodule

module Instruction_Decoder (
  input  [5:0] op_code,
  input  [5:0] func_code,
  output mfhi,
  output halt,
  output pop,
  output bne,
  output is_LH,
  output lw,
  output mflo,
  output tty,
  output push,
  output blez,
  output type_i,
  output sw,
  output nop,
  output rnd,
  output j,
  output bgtz,
  output is_ALU,
  output [3:0] ALU_selector,
  output jr,
  output kbd,
  output beq,
  output bltz,
  output ALU_type_i
);

  wire _000000, _111000, _111111, add, addi, \and , andi, comparator_1_eq, comparator_2_eq, comparator_3_eq,
       comparator_4_eq, comparator_6_eq, comparator_7_eq, comparator_8_eq, comparator_9_eq, comparator_10_eq,
       comparator_11_eq, comparator_18_eq, comparator_19_eq, comparator_20_eq, comparator_21_eq,
       comparator_26_eq, comparator_27_eq, comparator_28_eq, comparator_29_eq, comparator_35_eq,
       comparator_36_eq, comparator_37_eq, comparator_38_eq, div, divu, mult, mulu, \nor , \or , ori, slt,
       slti, sltu, sltui, sub, \xor , xori;

  Comparator #(.width(6)) comparator_1 (.a(6'b100000), .b(func_code), .eq(comparator_1_eq));  // open: gt, lt
  Comparator #(.width(6)) comparator_2 (.a(6'b100010), .b(func_code), .eq(comparator_2_eq));  // open: gt, lt
  Comparator #(.width(6)) comparator_3 (.a(6'b011000), .b(func_code), .eq(comparator_3_eq));  // open: gt, lt
  Comparator #(.width(6)) comparator_4 (.a(6'b011001), .b(func_code), .eq(comparator_4_eq));  // open: gt, lt
  and and_1 (add, _000000, comparator_1_eq);
  and and_2 (sub, _000000, comparator_2_eq);
  and and_3 (mult, _000000, comparator_3_eq);
  and and_4 (mulu, _000000, comparator_4_eq);
  Comparator #(.width(6)) comparator_5 (.a(6'b111000), .b(op_code), .eq(_111000));  // open: gt, lt
  and and_5 (pop, _111000, comparator_6_eq);
  Comparator #(.width(6)) comparator_6 (.a({6{1'b0}}), .b(func_code), .eq(comparator_6_eq));  // open: gt, lt
  and and_6 (push, _111000, comparator_7_eq);
  Comparator #(.width(6)) comparator_7 (.a(6'b000001), .b(func_code), .eq(comparator_7_eq));  // open: gt, lt
  Comparator #(.width(6)) comparator_8 (.a(6'b011010), .b(func_code), .eq(comparator_8_eq));  // open: gt, lt
  Comparator #(.width(6)) comparator_9 (.a(6'b011011), .b(func_code), .eq(comparator_9_eq));  // open: gt, lt
  Comparator #(.width(6)) comparator_10 (.a(6'b100100), .b(func_code), .eq(comparator_10_eq));  // open: gt, lt
  Comparator #(.width(6)) comparator_11 (.a(6'b100101), .b(func_code), .eq(comparator_11_eq));  // open: gt, lt
  ALU_Encoder alu_encoder_1 (
    .add(add), .addi(addi), .sub(sub), .slt(slt), .slti(slti), .sltu(sltu), .sltui(sltui), .\and (\and ),
    .andi(andi), .\or (\or ), .ori(ori), .\xor (\xor ), .xori(xori), .\nor (\nor ), .mult(mult), .mulu(mulu),
    .div(div), .divu(divu), .Selector(ALU_selector));
  Comparator #(.width(6)) comparator_12 (.a({6{1'b0}}), .b(op_code), .eq(_000000));  // open: gt, lt
  and and_7 (div, _000000, comparator_8_eq);
  and and_8 (divu, _000000, comparator_9_eq);
  and and_9 (\and , _000000, comparator_10_eq);
  and and_10 (\or , _000000, comparator_11_eq);
  Comparator #(.width(6)) comparator_13 (.a(6'b001000), .b(op_code), .eq(addi));  // open: gt, lt
  Comparator #(.width(6)) comparator_14 (.a(6'b001100), .b(op_code), .eq(andi));  // open: gt, lt
  Comparator #(.width(6)) comparator_15 (.a(6'b001101), .b(op_code), .eq(ori));  // open: gt, lt
  Comparator #(.width(6)) comparator_16 (.a(6'b001110), .b(op_code), .eq(xori));  // open: gt, lt
  Comparator #(.width(6)) comparator_17 (.a(6'b001010), .b(op_code), .eq(slti));  // open: gt, lt
  and and_11 (\nor , _000000, comparator_18_eq);
  Comparator #(.width(6)) comparator_18 (.a(6'b100111), .b(func_code), .eq(comparator_18_eq));  // open: gt, lt
  and and_12 (\xor , _000000, comparator_19_eq);
  Comparator #(.width(6)) comparator_19 (.a(6'b101000), .b(func_code), .eq(comparator_19_eq));  // open: gt, lt
  and and_13 (slt, _000000, comparator_20_eq);
  Comparator #(.width(6)) comparator_20 (.a(6'b101010), .b(func_code), .eq(comparator_20_eq));  // open: gt, lt
  and and_14 (sltu, _000000, comparator_21_eq);
  Comparator #(.width(6)) comparator_21 (.a(6'b101011), .b(func_code), .eq(comparator_21_eq));  // open: gt, lt
  Comparator #(.width(6)) comparator_22 (.a(6'b001011), .b(op_code), .eq(sltui));  // open: gt, lt
  Comparator #(.width(6)) comparator_23 (.a(6'b000100), .b(op_code), .eq(beq));  // open: gt, lt
  Comparator #(.width(6)) comparator_24 (.a(6'b000101), .b(op_code), .eq(bne));  // open: gt, lt
  Comparator #(.width(6)) comparator_25 (.a(6'b000110), .b(op_code), .eq(blez));  // open: gt, lt
  Comparator #(.width(6)) comparator_26 (.a(6'b010000), .b(func_code), .eq(comparator_26_eq));  // open: gt, lt
  Comparator #(.width(6)) comparator_27 (.a(6'b010010), .b(func_code), .eq(comparator_27_eq));  // open: gt, lt
  Comparator #(.width(6)) comparator_28 (.a({6{1'b0}}), .b(func_code), .eq(comparator_28_eq));  // open: gt, lt
  Comparator #(.width(6)) comparator_29 (.a(6'b001000), .b(func_code), .eq(comparator_29_eq));  // open: gt, lt
  and and_15 (mfhi, _000000, comparator_26_eq);
  and and_16 (mflo, _000000, comparator_27_eq);
  and and_17 (nop, _000000, comparator_28_eq);
  and and_18 (jr, _000000, comparator_29_eq);
  Comparator #(.width(6)) comparator_30 (.a(6'b000111), .b(op_code), .eq(bgtz));  // open: gt, lt
  Comparator #(.width(6)) comparator_31 (.a(6'b000001), .b(op_code), .eq(bltz));  // open: gt, lt
  Comparator #(.width(6)) comparator_32 (.a(6'b100011), .b(op_code), .eq(lw));  // open: gt, lt
  Comparator #(.width(6)) comparator_33 (.a(6'b101011), .b(op_code), .eq(sw));  // open: gt, lt
  or or_1 (is_ALU, add, \nor , \or , sltui, sub, \xor , addi, \and , slti, is_LH, sltu, slt, ALU_type_i);
  Comparator #(.width(6)) comparator_34 (.a({6{1'b1}}), .b(op_code), .eq(_111111));  // open: gt, lt
  Comparator #(.width(6)) comparator_35 (.a({6{1'b1}}), .b(func_code), .eq(comparator_35_eq));  // open: gt, lt
  Comparator #(.width(6)) comparator_36 (.a(6'b000001), .b(func_code), .eq(comparator_36_eq));  // open: gt, lt
  Comparator #(.width(6)) comparator_37 (.a(6'b000010), .b(func_code), .eq(comparator_37_eq));  // open: gt, lt
  Comparator #(.width(6)) comparator_38 (.a(6'b000100), .b(func_code), .eq(comparator_38_eq));  // open: gt, lt
  Comparator #(.width(6)) comparator_39 (.a(6'b000010), .b(op_code), .eq(j));  // open: gt, lt
  and and_19 (halt, _111111, comparator_35_eq);
  and and_20 (tty, _111111, comparator_36_eq);
  and and_21 (rnd, _111111, comparator_37_eq);
  and and_22 (kbd, _111111, comparator_38_eq);
  or or_2 (type_i, lw, bgtz, bne, sltui, xori, andi, addi, ori, slti, beq, blez, bltz, sw);
  or or_3 (ALU_type_i, xori, ori, andi);
  or or_4 (is_LH, mulu, div, mult, divu);

  // Notes on the sheet:
  //   Input
  //   Type R
  //   111000
  //   000000
  //   Type R
  //   INSTRUCTION DECODER
  //   Type I
  //   Outputs
  //   Type R
  //   111111
  //   Type J
endmodule

module Little_Endian___Big_Endian (
  input  [31:0] in_1,
  output [31:0] Output
);


  assign Output = {in_1[7:0], in_1[15:8], in_1[23:16], in_1[31:24]};

  // Notes on the sheet:
  //   Input
  //   LITTLE ENDIAN - BIG ENDIAN
  //   Output
endmodule

module Write_to_RAM (
  input  [31:0] dir_ram,
  input  [31:0] write_data,
  output [3:0] mask,
  output [15:0] RAM_A,
  output [31:0] bank_0,
  output [31:0] bank_1,
  output [31:0] bank_2,
  output [31:0] bank_3
);

  wire [31:0] little_endian_big_endian_1_output;

  Demultiplexer #(.select(2), .enable("false")) demultiplexer_1 (
    .out0(mask[0]), .out1(mask[1]), .out2(mask[2]), .out3(mask[3]), .in(1'b1), .sel(dir_ram[3:2]));
  Demultiplexer #(.select(2), .width(32), .enable("false")) demultiplexer_2 (
    .out0(bank_0), .out1(bank_1), .out2(bank_2), .out3(bank_3), .in(little_endian_big_endian_1_output),
    .sel(dir_ram[3:2]));
  Little_Endian___Big_Endian little_endian_big_endian_1 (.in_1(write_data), .Output(little_endian_big_endian_1_output));

  assign RAM_A = dir_ram[19:4];

  // Other names for the same wires on the sheet: selector[1:0] = dir_ram[3:2]

  // Notes on the sheet:
  //   Input
  //   WRITE TO RAM
  //   Output
endmodule

module Read_from_RAM (
  input  [31:0] bank_0,
  input  [31:0] bank_1,
  input  [31:0] bank_2,
  input  [31:0] bank_3,
  input  [31:0] dir_RAM,
  output [31:0] read_data
);

  wire [31:0] multiplexer_1_out;

  Multiplexer #(.select(2), .width(32), .enable("false")) multiplexer_1 (
    .in0(bank_0), .in1(bank_1), .in2(bank_2), .in3(bank_3), .out(multiplexer_1_out), .sel(dir_RAM[3:2]));
  Little_Endian___Big_Endian little_endian_big_endian_1 (.in_1(multiplexer_1_out), .Output(read_data));

  // Other names for the same wires on the sheet: selector[1:0] = dir_RAM[3:2]

  // Notes on the sheet:
  //   Input
  //   READ FROM RAM
  //   Output
endmodule
